// Logisim project ALU.circ as structural Verilog: 2 circuits, main circuit ALU
module ALU (
  input  [31:0] A,
  input  [31:0] B,
  input  [4:0] Shift,
  input  [3:0] Codop,
  input  CarryIn,
  output [3:0] Flags,
  output [31:0] S
);

  wire adder_1_cout, adder_2_cout, bitselector_1_out, bitselector_2_out, bitselector_3_out,
       bitselector_4_out, bitselector_5_out, bitselector_6_out, bitselector_7_out, bitselector_8_out,
       bitselector_9_out, bitselector_10_out, bitselector_11_out, not_1_out, not_3_out, not_4_out,
       subtractor_1_bout, subtractor_3_bout, table_res_perdu_1_entree_mux, Vadc, Vcmn, Vcmp, Vsbc,
       xnor_1_out, xor_2_out, xor_3_out, xor_4_out, xor_5_out, xor_6_out;
  wire [4:0] adder_3_out, subtractor_4_out;
  wire [31:0] D, E, F, G, H, I, J, K, L, M, multiplexer_1_out, O, P, Q, R, S_t, T;

  not not_1 (not_1_out, CarryIn);
  assign R = ~B;  // NOT_Gate not_2, 32 bits wide
  assign S_t = A & B;  // AND_Gate and_1, 32 bits wide
  assign D = A ^ B;  // XOR_Gate xor_1, 32 bits wide
  Shifter #(.width(32)) shifter_1 (.in(B), .\dist (Shift), .out(E));
  Shifter #(.shift("lr"), .width(32)) shifter_2 (.in(B), .\dist (Shift), .out(F));
  Shifter #(.shift("ar"), .width(32)) shifter_3 (.in(B), .\dist (Shift), .out(G));
  Adder #(.width(32)) adder_1 (.a(A), .b(B), .out(H), .cin(CarryIn), .cout(adder_1_cout));
  Subtractor #(.width(32)) subtractor_1 (.a(B), .b(A), .out(I), .bin(not_1_out), .bout(subtractor_1_bout));
  not not_3 (not_3_out, subtractor_1_bout);
  Shifter #(.shift("rr"), .width(32)) shifter_4 (.in(B), .\dist (Shift), .out(J));
  assign K = A & B;  // AND_Gate and_2, 32 bits wide
  Subtractor #(.width(32)) subtractor_2 (.a({32{1'b0}}), .b(A), .out(L));  // open: bin, bout
  Subtractor #(.width(32)) subtractor_3 (.a(B), .b(A), .out(M), .bout(subtractor_3_bout));  // open: bin
  Adder #(.width(32)) adder_2 (.a(A), .b(B), .out(T), .cout(adder_2_cout));  // open: cin
  assign O = A | B;  // OR_Gate or_1, 32 bits wide
  Multiplier #(.width(32)) multiplier_1 (.a(A), .b(B), .out(P));  // open: cin, cout
  assign Q = A & ~B;  // AND_Gate and_3, 32 bits wide
  not not_4 (not_4_out, subtractor_3_bout);
  Adder #(.width(5)) adder_3 (.a(Shift), .b(5'b00001), .out(adder_3_out));  // open: cin, cout
  Subtractor #(.width(5)) subtractor_4 (.a(Shift), .b(5'b00001), .out(subtractor_4_out));  // open: bin, bout
  Multiplexer #(.select(4), .width(32)) multiplexer_1 (
    .in0(S_t), .in1(D), .in2(E), .in3(F), .in4(G), .in5(H), .in6(I), .in7(J), .in8(K), .in9(L), .in10(M),
    .in11(T), .in12(O), .in13(P), .in14(Q), .in15(R), .out(multiplexer_1_out), .sel(Codop));  // open: en
  BitSelector #(.width(32)) bitselector_1 (.in(B), .out(bitselector_1_out), .sel(adder_3_out));
  BitSelector #(.width(32)) bitselector_2 (.in(B), .out(bitselector_2_out), .sel(subtractor_4_out));
  BitSelector #(.width(32)) bitselector_3 (.in(B), .out(bitselector_3_out), .sel({5{1'b1}}));
  Multiplexer #(.select(4)) multiplexer_2 (
    .in0(1'b0), .in1(1'b0), .in2(bitselector_1_out), .in3(bitselector_2_out), .in4(bitselector_2_out),
    .in5(adder_1_cout), .in6(not_3_out), .in7(bitselector_3_out), .in8(1'b0), .in9(1'b0), .in10(not_4_out),
    .in11(adder_2_cout), .in12(1'b0), .in13(1'b0), .in14(1'b0), .in15(1'b0), .out(Flags[1]), .sel(Codop));  // open: en
  table_res_perdu table_res_perdu_1 (.codop(Codop), .entree_mux(table_res_perdu_1_entree_mux));
  BitSelector #(.width(32)) bitselector_4 (.in(H), .out(bitselector_4_out), .sel({5{1'b1}}));
  BitSelector #(.width(32)) bitselector_5 (.in(T), .out(bitselector_5_out), .sel({5{1'b1}}));
  Comparator #(.width(32)) comparator_1 (
    .a(multiplexer_1_out), .b({32{1'b0}}), .eq(Flags[2]), .lt(Flags[3]));  // open: gt
  Multiplexer #(.width(32)) multiplexer_3 (
    .in0(multiplexer_1_out), .in1(B), .out(S), .sel(table_res_perdu_1_entree_mux));  // open: en
  BitSelector #(.width(32)) bitselector_6 (.in(A), .out(bitselector_6_out), .sel({5{1'b1}}));
  BitSelector #(.width(32)) bitselector_7 (.in(B), .out(bitselector_7_out), .sel({5{1'b1}}));
  BitSelector #(.width(32)) bitselector_8 (.in(B), .out(bitselector_8_out), .sel({5{1'b1}}));
  xnor xnor_1 (xnor_1_out, bitselector_6_out, bitselector_7_out);
  xor xor_2 (xor_2_out, bitselector_7_out, bitselector_4_out);
  xor xor_3 (xor_3_out, bitselector_7_out, bitselector_5_out);
  BitSelector #(.width(32)) bitselector_9 (.in(A), .out(bitselector_9_out), .sel({5{1'b1}}));
  BitSelector #(.width(32)) bitselector_10 (.in(M), .out(bitselector_10_out), .sel({5{1'b1}}));
  BitSelector #(.width(32)) bitselector_11 (.in(I), .out(bitselector_11_out), .sel({5{1'b1}}));
  xor xor_4 (xor_4_out, bitselector_9_out, bitselector_8_out);
  xor xor_5 (xor_5_out, bitselector_8_out, bitselector_10_out);
  xor xor_6 (xor_6_out, bitselector_8_out, bitselector_11_out);
  and and_4 (Vadc, xnor_1_out, xor_2_out);
  and and_5 (Vcmn, xnor_1_out, xor_3_out);
  and and_6 (Vcmp, xor_4_out, xor_5_out);
  and and_7 (Vsbc, xor_4_out, xor_6_out);
  Multiplexer #(.select(4)) multiplexer_4 (
    .in0(1'b0), .in1(1'b0), .in2(1'b0), .in3(1'b0), .in4(1'b0), .in5(Vadc), .in6(Vsbc), .in7(1'b0),
    .in8(1'b0), .in9(1'b0), .in10(Vcmp), .in11(Vcmn), .in12(1'b0), .in14(1'b0), .in15(1'b0), .out(Flags[0]),
    .sel(Codop));  // open: in13, en

  // Other names for the same wires on the sheet: Cin = CarryIn; COp[3:0] = Codop; V = Flags[0]; C = Flags[1];
  //   Z = Flags[2]; N = Flags[3]

  // Notes on the sheet:
  //   Note: for ROR, C = N
  //   Note 2: assume that shift > 0 for LSL and LSR
endmodule

module table_res_perdu (
  input  [3:0] codop,
  output entree_mux
);

  wire and_1_out, and_2_out, not_1_out, not_2_out;

  not not_1 (not_1_out, codop[2]);
  not not_2 (not_2_out, codop[0]);
  and and_1 (and_1_out, codop[3], not_1_out, not_2_out);
  and and_2 (and_2_out, codop[3], not_1_out, codop[1]);
  or or_1 (entree_mux, and_1_out, and_2_out);
endmodule
