// Logisim project Ctl_Conditional.circ as structural Verilog: 1 circuit, main circuit Conditional
module Conditional (
  input  Enable,
  input  [15:0] Instruction,
  input  Z,
  input  C,
  input  N,
  input  V,
  output [10:0] Offset,
  output Verified
);

  wire and_10_out, and_12_out, and_16_out, and_18_out, and_19_out, comparator_1_eq, comparator_2_eq,
       comparator_3_eq, comparator_4_eq, comparator_5_eq, comparator_6_eq, comparator_7_eq, comparator_8_eq,
       comparator_9_eq, comparator_10_eq, comparator_11_eq, comparator_12_eq, comparator_13_eq,
       comparator_14_eq, comparator_15_eq, comparator_16_eq, comparator_17_eq, comparator_18_eq,
       comparator_19_eq, comparator_20_eq, comparator_21_eq, comparator_22_eq, comparator_23_eq,
       comparator_24_eq, comparator_25_eq, comparator_26_eq, comparator_27_eq, comparator_28_eq,
       comparator_29_eq, comparator_30_eq, comparator_31_eq, comparator_32_eq, not_1_out, not_2_out, ok1, ok2;

  Comparator #(.width(4)) comparator_1 (.a(Instruction[11:8]), .b(4'b0000), .eq(comparator_1_eq));  // open: gt, lt
  Comparator #(.width(1)) comparator_2 (.a(Z), .b(1'b1), .eq(comparator_2_eq));  // open: gt, lt
  Comparator #(.width(4)) comparator_3 (.a(Instruction[11:8]), .b(4'b0001), .eq(comparator_3_eq));  // open: gt, lt
  Comparator #(.width(1)) comparator_4 (.a(Z), .b(1'b0), .eq(comparator_4_eq));  // open: gt, lt
  Comparator #(.width(4)) comparator_5 (.a(Instruction[11:8]), .b(4'b0010), .eq(comparator_5_eq));  // open: gt, lt
  Comparator #(.width(1)) comparator_6 (.a(C), .b(1'b1), .eq(comparator_6_eq));  // open: gt, lt
  Comparator #(.width(4)) comparator_7 (.a(Instruction[11:8]), .b(4'b0011), .eq(comparator_7_eq));  // open: gt, lt
  Comparator #(.width(1)) comparator_8 (.a(C), .b(1'b0), .eq(comparator_8_eq));  // open: gt, lt
  Comparator #(.width(4)) comparator_9 (.a(Instruction[11:8]), .b(4'b0100), .eq(comparator_9_eq));  // open: gt, lt
  Comparator #(.width(1)) comparator_10 (.a(N), .b(1'b1), .eq(comparator_10_eq));  // open: gt, lt
  Comparator #(.width(4)) comparator_11 (.a(Instruction[11:8]), .b(4'b0101), .eq(comparator_11_eq));  // open: gt, lt
  Comparator #(.width(1)) comparator_12 (.a(N), .b(1'b0), .eq(comparator_12_eq));  // open: gt, lt
  Comparator #(.width(4)) comparator_13 (.a(Instruction[11:8]), .b(4'b0110), .eq(comparator_13_eq));  // open: gt, lt
  Comparator #(.width(1)) comparator_14 (.a(V), .b(1'b1), .eq(comparator_14_eq));  // open: gt, lt
  Comparator #(.width(4)) comparator_15 (.a(Instruction[11:8]), .b(4'b0111), .eq(comparator_15_eq));  // open: gt, lt
  Comparator #(.width(1)) comparator_16 (.a(V), .b(1'b0), .eq(comparator_16_eq));  // open: gt, lt
  Comparator #(.width(4)) comparator_17 (.a(Instruction[11:8]), .b(4'b1000), .eq(comparator_17_eq));  // open: gt, lt
  Comparator #(.width(1)) comparator_18 (.a(C), .b(1'b1), .eq(comparator_18_eq));  // open: gt, lt
  Comparator #(.width(1)) comparator_19 (.a(Z), .b(1'b0), .eq(comparator_19_eq));  // open: gt, lt
  Comparator #(.width(4)) comparator_20 (.a(Instruction[11:8]), .b(4'b1001), .eq(comparator_20_eq));  // open: gt, lt
  Comparator #(.width(1)) comparator_21 (.a(C), .b(1'b0), .eq(comparator_21_eq));  // open: gt, lt
  Comparator #(.width(1)) comparator_22 (.a(Z), .b(1'b1), .eq(comparator_22_eq));  // open: gt, lt
  Comparator #(.width(4)) comparator_23 (.a(Instruction[11:8]), .b(4'b1010), .eq(comparator_23_eq));  // open: gt, lt
  Comparator #(.width(1)) comparator_24 (.a(V), .b(N), .eq(comparator_24_eq));  // open: gt, lt
  Comparator #(.width(4)) comparator_25 (.a(Instruction[11:8]), .b(4'b1011), .eq(comparator_25_eq));  // open: gt, lt
  not not_1 (not_1_out, comparator_26_eq);
  Comparator #(.width(1)) comparator_26 (.a(V), .b(N), .eq(comparator_26_eq));  // open: gt, lt
  Comparator #(.width(4)) comparator_27 (.a(Instruction[11:8]), .b(4'b1100), .eq(comparator_27_eq));  // open: gt, lt
  Comparator #(.width(1)) comparator_28 (.a(N), .b(V), .eq(comparator_28_eq));  // open: gt, lt
  Comparator #(.width(1)) comparator_29 (.a(Z), .b(1'b0), .eq(comparator_29_eq));  // open: gt, lt
  Comparator #(.width(4)) comparator_30 (.a(Instruction[11:8]), .b(4'b1101), .eq(comparator_30_eq));  // open: gt, lt
  not not_2 (not_2_out, comparator_31_eq);
  Comparator #(.width(1)) comparator_31 (.a(N), .b(V), .eq(comparator_31_eq));  // open: gt, lt
  Comparator #(.width(1)) comparator_32 (.a(Z), .b(1'b1), .eq(comparator_32_eq));  // open: gt, lt
  Comparator #(.width(4)) comparator_33 (.a(Instruction[11:8]), .b(4'b1110), .eq(ok2));  // open: gt, lt
  and and_1 (ok2, comparator_1_eq, comparator_2_eq);
  and and_2 (ok2, comparator_3_eq, comparator_4_eq);
  and and_3 (ok2, comparator_5_eq, comparator_6_eq);
  and and_4 (ok2, comparator_7_eq, comparator_8_eq);
  and and_5 (ok2, comparator_9_eq, comparator_10_eq);
  and and_6 (ok2, comparator_11_eq, comparator_12_eq);
  and and_7 (ok2, comparator_13_eq, comparator_14_eq);
  and and_8 (ok2, comparator_15_eq, comparator_16_eq);
  and and_9 (ok2, comparator_17_eq, and_10_out);
  and and_10 (and_10_out, comparator_18_eq, comparator_19_eq);
  and and_11 (ok2, comparator_20_eq, and_12_out);
  and and_12 (and_12_out, comparator_21_eq, comparator_22_eq);
  and and_13 (ok2, comparator_23_eq, comparator_24_eq);
  and and_14 (ok2, comparator_25_eq, not_1_out);
  and and_15 (ok2, comparator_27_eq, and_16_out);
  and and_16 (and_16_out, comparator_28_eq, comparator_29_eq);
  and and_17 (ok2, comparator_30_eq, and_18_out);
  and and_18 (and_18_out, not_2_out, comparator_32_eq);
  Comparator #(.width(4)) comparator_34 (.a(Instruction[15:12]), .b(4'b1101), .eq(ok1));  // open: gt, lt
  and and_19 (and_19_out, ok1, ok2);
  assign Verified = Enable ? and_19_out : 1'bz;  // Controlled_Buffer controlled_buffer_1

  // Other names for the same wires on the sheet: Cond[3:0] = Instruction[11:8]; EN = Enable;
  //   imm8[7:0] = Instruction[7:0]

  // Notes on the sheet:
  //   égalité
  //   différence
  //   retenue
  //   négatif
  //   pas de retenue
  //   positif ou nul
  //   dépassement de capacité
  //   pas de dépassement de capacité
  //   supérieur non signé
  //   inf ou égal non signé
  //   inf ou égal signé
  //   inf signé
  //   sup signé
  //   inf ou égal signé
  //   inf ou égal signé
endmodule
