// Logisim project Ctl_Data_Processing.circ as structural Verilog: 2 circuits, main circuit ALU
module Data_Processing (
  input  Enable,
  input  [15:0] Instruction,
  output [2:0] Rd,
  output [2:0] Rn,
  output [2:0] Rm,
  output [3:0] ALU_Opcode,
  output [3:0] Flags_Update_Mask
);

  wire [2:0] D, M;
  wire [3:0] al, mask;

  BitSelector #(.group(3), .width(16)) bitselector_1 (.in(Instruction), .out(al[2:0]), .sel(3'b010));
  BitSelector #(.width(16)) bitselector_2 (.in(Instruction), .out(al[3]), .sel(4'b1001));
  BitSelector #(.group(3), .width(16)) bitselector_3 (.in(Instruction), .out(D), .sel(3'b000));
  BitSelector #(.group(3), .width(16)) bitselector_4 (.in(Instruction), .out(M), .sel(3'b001));
  assign Rd = Enable ? D : 3'bz;  // Controlled_Buffer controlled_buffer_1
  assign Rn = Enable ? D : 3'bz;  // Controlled_Buffer controlled_buffer_2
  assign Rm = Enable ? M : 3'bz;  // Controlled_Buffer controlled_buffer_3
  assign ALU_Opcode = Enable ? al : 4'bz;  // Controlled_Buffer controlled_buffer_4
  assign Flags_Update_Mask = Enable ? mask : 4'bz;  // Controlled_Buffer controlled_buffer_5
  Pull_Resistor pull_resistor_1 (.node(Rd));
  Pull_Resistor pull_resistor_2 (.node(Rn));
  Pull_Resistor pull_resistor_3 (.node(Rm));
  Pull_Resistor pull_resistor_4 (.node(ALU_Opcode));
  Pull_Resistor pull_resistor_5 (.node(Flags_Update_Mask));
  Multiplexer #(.enable("false"), .select(4), .width(4)) multiplexer_1 (
    .in0(4'b1110), .in1(4'b1110), .in2(4'b1110), .in3(4'b1110), .in4(4'b1110), .in5(4'b1111), .in6(4'b1111),
    .in7(4'b1110), .in8(4'b1110), .in9(4'b1111), .in10(4'b1111), .in11(4'b1111), .in12(4'b1110),
    .in13(4'b1100), .in14(4'b1110), .in15(4'b1110), .out(mask), .sel(al));

  // Other names for the same wires on the sheet: I[15:0] = Instruction; N[2:0] = D

  // Notes on the sheet:
  //   Note 2: RSB instruction has Rn as 1st operand.
  //   MUL instruction has Rn as 1st operand and Rdm as 2nd operand
  //   For simplification purposes, Rm is used for 1st operand both here and in the ALU.
  //   Note: instructions that does not save the result will still have the second operand as the destination register, the ALU will copy the second register to the destination register
  //   Pull output low on Enable = 0
endmodule

module ALU (
  input  [31:0] A,
  input  [31:0] B,
  input  [4:0] Shift,
  input  [3:0] Codop,
  input  CarryIn,
  output [31:0] S,
  output [3:0] Flags
);

  wire adder_1_cout, adder_2_cout, bitselector_1_out, bitselector_2_out, bitselector_6_out,
       bitselector_7_out, bitselector_8_out, bitselector_9_out, C2, C3, C8, dernierBitEgale,
       subtractor_1_bout, subtractor_2_bout, subtractor_3_bout, V5, V6, V10, V11;
  wire [4:0] adder_3_out, subtractor_5_out;
  wire [31:0] D, E, F, G, H, I, J, K, L, M, not_1_out, O, P, Q, R, S_t, subtractor_1_out, T;

  assign not_1_out = ~B;  // NOT_Gate not_1, 32 bits wide
  assign R = ~B;  // NOT_Gate not_2, 32 bits wide
  assign D = A ^ A;  // XOR_Gate xor_1, 32 bits wide
  Shifter #(.width(32)) shifter_1 (.in(B), .\dist (Shift), .out(E));
  Shifter #(.shift("lr"), .width(32)) shifter_2 (.in(B), .\dist (Shift), .out(F));
  Shifter #(.shift("ar"), .width(32)) shifter_3 (.in(B), .\dist (Shift), .out(G));
  Adder #(.width(32)) adder_1 (.a(A), .b(B), .out(H), .cin(CarryIn), .cout(adder_1_cout));
  Subtractor #(.width(32)) subtractor_1 (.a(A), .b(B), .out(subtractor_1_out), .bin(CarryIn), .bout(subtractor_1_bout));
  Shifter #(.shift("rr"), .width(32)) shifter_4 (.in(B), .\dist (Shift), .out(J));
  Subtractor #(.width(32)) subtractor_2 (.a({32{1'b0}}), .b(A), .out(L), .bout(subtractor_2_bout));  // open: bin
  Subtractor #(.width(32)) subtractor_3 (.a(A), .b(B), .out(M), .bout(subtractor_3_bout));  // open: bin
  Adder #(.width(32)) adder_2 (.a(A), .b(B), .out(T), .cout(adder_2_cout));  // open: cin
  Multiplier #(.width(32)) multiplier_1 (.a(A), .b(B), .out(P));  // open: cin, cout
  assign S_t = A & A;  // AND_Gate and_1, 32 bits wide
  assign K = A & B;  // AND_Gate and_2, 32 bits wide
  assign O = A | B;  // OR_Gate or_1, 32 bits wide
  assign Q = A & not_1_out;  // AND_Gate and_3, 32 bits wide
  Multiplexer #(.enable("false"), .select(4), .width(32)) multiplexer_1 (
    .in0(S_t), .in1(D), .in2(E), .in3(F), .in4(G), .in5(H), .in6(I), .in7(J), .in8(K), .in9(L), .in10(M),
    .in11(T), .in12(O), .in13(P), .in14(Q), .in15(R), .out(S), .sel(Codop));
  Subtractor #(.width(32)) subtractor_4 (.a(subtractor_1_out), .b(32'h1), .out(I));  // open: bin, bout
  Multiplexer #(.enable("false"), .select(4)) multiplexer_2 (
    .in0(1'b0), .in1(1'b0), .in2(C2), .in3(C3), .in4(C3), .in5(adder_1_cout), .in6(subtractor_1_bout),
    .in7(C8), .in8(1'b0), .in9(subtractor_2_bout), .in10(subtractor_3_bout), .in11(adder_2_cout),
    .in12(1'b0), .in13(1'b0), .in14(1'b0), .in15(1'b0), .out(Flags[2]), .sel(Codop));
  Comparator #(.width(32)) comparator_1 (.a(S), .b({32{1'b0}}), .eq(Flags[1]), .lt(Flags[0]));  // open: gt
  Multiplexer #(.enable("false"), .select(4)) multiplexer_3 (
    .in0(1'b0), .in1(1'b0), .in2(1'b0), .in3(1'b0), .in4(1'b0), .in5(V5), .in6(V6), .in7(1'b0), .in8(1'b0),
    .in9(1'b0), .in10(V10), .in11(V11), .in12(1'b0), .in13(1'b0), .in14(1'b0), .in15(1'b0), .out(Flags[3]),
    .sel(Codop));
  BitSelector #(.width(32)) bitselector_1 (.in(A), .out(bitselector_1_out), .sel({5{1'b1}}));
  BitSelector #(.width(32)) bitselector_2 (.in(B), .out(bitselector_2_out), .sel({5{1'b1}}));
  and and_4 (dernierBitEgale, bitselector_1_out, bitselector_2_out);
  BitSelector #(.width(32)) bitselector_3 (.in(B), .out(C2), .sel(adder_3_out));
  Adder #(.width(5)) adder_3 (.a(Shift), .b(5'b00001), .out(adder_3_out));  // open: cin, cout
  BitSelector #(.width(32)) bitselector_4 (.in(B), .out(C3), .sel(subtractor_5_out));
  Subtractor #(.width(5)) subtractor_5 (.a(Shift), .b(5'b00001), .out(subtractor_5_out));  // open: bin, bout
  BitSelector #(.width(32)) bitselector_5 (.in(B), .out(C8), .sel({5{1'b1}}));
  BitSelector #(.width(32)) bitselector_6 (.in(T), .out(bitselector_6_out), .sel({5{1'b1}}));
  BitSelector #(.width(32)) bitselector_7 (.in(H), .out(bitselector_7_out), .sel({5{1'b1}}));
  BitSelector #(.width(32)) bitselector_8 (.in(M), .out(bitselector_8_out), .sel({5{1'b1}}));
  BitSelector #(.width(32)) bitselector_9 (.in(I), .out(bitselector_9_out), .sel({5{1'b1}}));
  xor xor_2 (V5, dernierBitEgale, bitselector_6_out);
  xor xor_3 (V11, dernierBitEgale, bitselector_7_out);
  xor xor_4 (V10, dernierBitEgale, bitselector_8_out);
  xor xor_5 (V6, dernierBitEgale, bitselector_9_out);

  // Other names for the same wires on the sheet: C4 = C3; Cin = CarryIn; COp[3:0] = Codop; N = Flags[0]; Z = Flags[1];
  //   C = Flags[2]; V = Flags[3]

  // Notes on the sheet:
  //   Note: for ROR, C = N
  //   Note 2: assume that shift > 0 for LSL and LSR
endmodule
