// Logisim project Ctl_Flags_APSR.circ as structural Verilog: 1 circuit, main circuit Flags_APSR
module Flags_APSR (
  input  [3:0] Update_Mask,
  input  [3:0] Flags_In,
  input  Rst,
  input  Clk,
  output [3:0] Flags_Out
);

  wire [3:0] adder_1_out, not_1_out, or_1_out, or_2_out;

  assign not_1_out = ~Update_Mask;  // NOT_Gate not_1, 4 bits wide
  assign or_1_out = Update_Mask | Flags_In;  // OR_Gate or_1, 4 bits wide
  assign or_2_out = not_1_out | Flags_Out;  // OR_Gate or_2, 4 bits wide
  Adder #(.width(4)) adder_1 (.a(or_1_out), .b(or_2_out), .out(adder_1_out));  // open: cin, cout
  Register #(.width(4)) register_1 (.D(adder_1_out), .en(1'b1), .clk(Rst), .Q(Flags_Out), .clr(Clk));

  // Other names for the same wires on the sheet: FLout[3:0] = Flags_Out
endmodule
