// Logisim project Ctl_Load_Store.circ as structural Verilog: 1 circuit, main circuit Load_Store
module Load_Store (
  input  [15:0] Instruction,
  input  Enable,
  input  Clk,
  input  Reset,
  input  [31:0] Stack_Pointer,
  output Store,
  output Load,
  output PC_Hold,
  output [2:0] Rmd,
  output [31:0] RAM_Addr
);

  wire and_1_out, d_ff_1_q, Load_t, PC_Hold_t, Store_t;
  wire [2:0] Rmd_t;
  wire [7:0] shifter_1_out;
  wire [31:0] bit_extender_1_out, RAM_Addr_t;

  Decoder decoder_1 (.out0(Store_t), .out1(Load_t), .sel(Instruction[11]));  // open: en
  Shifter shifter_1 (.in(Instruction[7:0]), .\dist (3'b010), .out(shifter_1_out));
  assign bit_extender_1_out = {{24{shifter_1_out[7]}}, shifter_1_out};  // Bit_Extender bit_extender_1
  Adder #(.width(32)) adder_1 (.a(bit_extender_1_out), .b(Stack_Pointer), .out(RAM_Addr_t));  // open: cin, cout
  D_Flip_Flop d_ff_1 (.D(and_1_out), .clk(Clk), .Q(d_ff_1_q), .reset(Reset));  // open: Qn, preset
  and and_1 (and_1_out, d_ff_1_q, Instruction[11]);
  assign Store = Enable ? Store_t : 1'bz;  // Controlled_Buffer controlled_buffer_1
  Pull_Resistor pull_resistor_1 (.node(Store));
  assign Load = Enable ? Load_t : 1'bz;  // Controlled_Buffer controlled_buffer_2
  Pull_Resistor pull_resistor_2 (.node(Load));
  assign PC_Hold = Enable ? PC_Hold_t : 1'bz;  // Controlled_Buffer controlled_buffer_3
  Pull_Resistor pull_resistor_3 (.node(PC_Hold));
  assign Rmd = Enable ? Rmd_t : 3'bz;  // Controlled_Buffer controlled_buffer_4
  Pull_Resistor pull_resistor_4 (.node(Rmd));
  assign RAM_Addr = Enable ? RAM_Addr_t : 32'bz;  // Controlled_Buffer controlled_buffer_5
  Pull_Resistor pull_resistor_5 (.node(RAM_Addr));
  and and_2 (Load_t, Instruction[11], d_ff_1_q);
  and and_3 (PC_Hold_t, d_ff_1_q, Instruction[11]);

  // Other names for the same wires on the sheet: imm8[7:0] = Instruction[7:0]; Ins[15:0] = Instruction;
  //   Rt[2:0] = Instruction[10:8]; PremierBit = Instruction[11]; Rst = Reset; SP[31:0] = Stack_Pointer

  // Notes on the sheet:
  //   Instruction: pull=down
  //   Delay load and hold PC for 1 cycle for the RAM to send out requested data 
endmodule
