// Logisim project Ctl_Opcode_Decoder.circ as structural Verilog: 2 circuits, main circuit Opcode_Decoder
module Opcode_Decoder (
  input  [5:0] Opcode,
  output Shift,
  output Data_Processing,
  output Load_Store,
  output SP_Address,
  output Conditional
);

  opcode_table opcode_table_1 (
    .opcode(Opcode), .shift(Shift), .data_processing(Data_Processing), .load_store(Load_Store),
    .sp_address(SP_Address), .branch(Conditional));

  // Notes on the sheet:
  //   Shift, add, sub, mov
  //   Data Processing
  //   Load/Store
  //   SP Address
  //   Conditional branch
endmodule

module opcode_table (
  input  [5:0] opcode,
  output shift,
  output data_processing,
  output load_store,
  output sp_address,
  output branch
);

  wire and_5_out, and_6_out, not_1_out, not_2_out, not_3_out, not_4_out, not_5_out, not_6_out;

  not not_1 (not_1_out, opcode[5]);
  not not_2 (not_2_out, opcode[4]);
  not not_3 (not_3_out, opcode[3]);
  not not_4 (not_4_out, opcode[2]);
  not not_5 (not_5_out, opcode[1]);
  not not_6 (not_6_out, opcode[0]);
  and and_1 (shift, not_1_out, not_2_out);
  and and_2 (data_processing, not_1_out, opcode[4], not_3_out, not_4_out, not_5_out, not_6_out);
  and and_3 (load_store, opcode[5], not_2_out, not_3_out, opcode[2]);
  and and_4 (sp_address, opcode[5], not_2_out, opcode[3], opcode[2]);
  and and_5 (and_5_out, opcode[5], opcode[4], not_3_out, opcode[2]);
  and and_6 (and_6_out, opcode[5], opcode[4], opcode[3], not_4_out, not_5_out);
  or or_1 (branch, and_5_out, and_6_out);
endmodule
